// Logisim project 4 bit adder subtractor.circ as structural Verilog: 1 circuit, main circuit main
module main (
  input  [3:0] Input_A,
  input  [3:0] Input_B,
  input  in_3,
  output out_4,
  output out_5,
  output out_6,
  output out_7,
  output Carry_output
);

  wire adder_1_cout, adder_2_cout, adder_3_cout, xor_1_out, xor_2_out, xor_3_out, xor_4_out;

  xor xor_1 (xor_1_out, Input_B[0], in_3);
  xor xor_2 (xor_2_out, Input_B[1], in_3);
  xor xor_3 (xor_3_out, Input_B[2], in_3);
  xor xor_4 (xor_4_out, Input_B[3], in_3);
  Adder #(.width(1)) adder_1 (.a(Input_A[0]), .b(xor_1_out), .out(out_4), .cin(in_3), .cout(adder_1_cout));
  Adder #(.width(1)) adder_2 (.a(Input_A[1]), .b(xor_2_out), .out(out_5), .cin(adder_1_cout), .cout(adder_2_cout));
  Adder #(.width(1)) adder_3 (.a(Input_A[2]), .b(xor_3_out), .out(out_6), .cin(adder_2_cout), .cout(adder_3_cout));
  Adder #(.width(1)) adder_4 (.a(Input_A[3]), .b(xor_4_out), .out(out_7), .cin(adder_3_cout), .cout(Carry_output));
endmodule
