// Logisim project 4 bit adder.circ as structural Verilog: 1 circuit, main circuit main
module main (
  input  in_1,
  input  [3:0] Input_A,
  input  [3:0] Input_B,
  output out_4,
  output out_5,
  output out_6,
  output out_7,
  output carry_bit_output
);

  wire adder_1_cout, adder_2_cout, adder_3_cout;

  Adder #(.width(1)) adder_1 (.a(Input_A[0]), .b(Input_B[0]), .out(out_4), .cin(in_1), .cout(adder_1_cout));
  Adder #(.width(1)) adder_2 (.a(Input_A[1]), .b(Input_B[1]), .out(out_5), .cin(adder_1_cout), .cout(adder_2_cout));
  Adder #(.width(1)) adder_3 (.a(Input_A[2]), .b(Input_B[2]), .out(out_6), .cin(adder_2_cout), .cout(adder_3_cout));
  Adder #(.width(1)) adder_4 (.a(Input_A[3]), .b(Input_B[3]), .out(out_7), .cin(adder_3_cout), .cout(carry_bit_output));

  // Notes on the sheet:
  //   4 bit adder
endmodule
