// Logisim project 4 bit alu.circ as structural Verilog: 1 circuit, main circuit main
module main (
  input  Cin,
  input  [3:0] A,
  input  [1:0] Select,
  input  [3:0] B,
  input  in_5,
  output out_6,
  output out_7,
  output out_8,
  output out_9,
  output out_10
);

  wire adder_1_cout, adder_2_cout, adder_3_cout, multiplexer_1_out, multiplexer_2_out, multiplexer_3_out,
       multiplexer_4_out, not_1_out, not_2_out, not_3_out, not_4_out, not_5_out;

  not not_1 (not_1_out, in_5);
  not not_2 (not_2_out, B[0]);
  not not_3 (not_3_out, B[1]);
  not not_4 (not_4_out, B[2]);
  not not_5 (not_5_out, B[3]);
  Multiplexer #(.select(2)) multiplexer_1 (
    .in0(B[0]), .in1(not_2_out), .in2(in_5), .in3(not_1_out), .out(multiplexer_1_out), .sel(Select));  // open: en
  Multiplexer #(.select(2)) multiplexer_2 (
    .in0(B[1]), .in1(not_3_out), .in2(in_5), .in3(not_1_out), .out(multiplexer_2_out), .sel(Select));  // open: en
  Multiplexer #(.select(2)) multiplexer_3 (
    .in0(B[2]), .in1(not_4_out), .in2(in_5), .in3(not_1_out), .out(multiplexer_3_out), .sel(Select));  // open: en
  Multiplexer #(.select(2)) multiplexer_4 (
    .in0(B[3]), .in1(not_5_out), .in2(in_5), .in3(not_1_out), .out(multiplexer_4_out), .sel(Select));  // open: en
  Adder #(.width(1)) adder_1 (.a(A[0]), .b(multiplexer_1_out), .out(out_6), .cin(Cin), .cout(adder_1_cout));
  Adder #(.width(1)) adder_2 (.a(A[1]), .b(multiplexer_2_out), .out(out_7), .cin(adder_1_cout), .cout(adder_2_cout));
  Adder #(.width(1)) adder_3 (.a(A[2]), .b(multiplexer_3_out), .out(out_8), .cin(adder_2_cout), .cout(adder_3_cout));
  Adder #(.width(1)) adder_4 (.a(A[3]), .b(multiplexer_4_out), .out(out_9), .cin(adder_3_cout), .cout(out_10));
endmodule
